// Logisim project dl.10.circ as structural Verilog: 1 circuit, main circuit main
module main (
  input  in_1,
  input  in_2,
  input  in_3,
  output Difference,
  output Borrow
);

  wire and_1_out, and_2_out, not_1_out, xor_1_out;

  xor xor_1 (xor_1_out, in_1, in_2);
  not not_1 (not_1_out, xor_1_out);
  xor xor_2 (Difference, xor_1_out, in_2);
  and and_1 (and_1_out, not_1_out, in_3);
  and and_2 (and_2_out, in_1, in_2);
  or or_1 (Borrow, and_1_out, and_2_out);
endmodule
